# Fritzing sketch power-channel-p (saved by Fritzing 0.9.6b)
breadboards: 1

parts:
  R1 = Resistor [tolerance=±5% resistance=150k package=THT]
  R2 = Resistor [tolerance=±5% resistance=680k package=THT]
  Q1 = Basic FET P-Channel [package="TO220 [THT]"]
  J1 = Screw terminal - 2 pins [package=THT]
  Q2 = NPN-Transistor [package="TO92 [THT]"]
  R3 = Resistor [tolerance=±5% resistance=150k package=THT]
  R4 = Resistor [tolerance=±5% resistance=150k package=THT]
  Q3 = NPN-Transistor [package="TO92 [THT]"]
  R5 = Resistor [tolerance=±5% resistance=10k package=THT]
  J3 = Screw terminal - 2 pins [package=THT]
  R6 = Resistor [tolerance=±5% resistance=10k package=THT]
  J4 = Screw terminal - 2 pins [package=THT]
  J5 = Screw terminal - 2 pins [package=THT]
  D1 = Rectifier Diode [part_number=1N4001 package="300 mil [THT]"]
  U1 = Voltage Regulator - 5V [package="TO220 [THT]"]
  C1 = Electrolytic Capacitor [capacitance=1µF voltage=35V package="100 mil [THT, electrolytic]"]
  D2 = Rectifier Diode [part_number=1N4001 package="300 mil [THT]"]

nets:
  N1: R1.Pin_0, Q1.source, J1.pin1
  N2: R1.Pin_1, R2.Pin_0, Q1.gate
  N3: R2.Pin_1, Q2.C
  N4: Q1.drain, J4.pin2, D1.cathode, U1.input_voltage, D2.anode
  GND: J1.pin2, Q2.E, Q3.E, D1.anode, U1.GND, C1.-
  N5: Q2.B, R4.Pin_1, R6.Pin_0
  N6: R3.Pin_0, J4.pin1, D2.cathode
  N7: R3.Pin_1, R4.Pin_0, Q3.C, J3.pin2
  N8: Q3.B, R5.Pin_0
  N9: R5.Pin_1, J3.pin1
  N10: R6.Pin_1, J5.pin1
  N11: J5.pin2, U1.output_voltage, C1.+

notes:
  +36V
  +5V
  charger
  button
  battery
  micro
